// Logisim project Bekzat_Kabdrashev_Lab1.circ as structural Verilog: 1 circuit, main circuit main
module main (
  input  Sel,
  input  In1,
  input  In2,
  output Out1
);

  wire and_1_out, and_2_out, not_1_out;

  not not_1 (not_1_out, Sel);
  and and_1 (and_1_out, Sel, In1);
  and and_2 (and_2_out, not_1_out, In2);
  or or_1 (Out1, and_1_out, and_2_out);

  // Notes on the sheet:
  //   December 15, 2025
  //   Bekzat Kabdrashev
  //   Lab 01: 2-Way, 1-Bit Multiplexer
  //   Chip Design Bootcamp 2025
endmodule
