// Logisim project Bekzat_Kabdrashev_Lab5.circ as structural Verilog: 7 circuits, main circuit main
module main (
  input  Reset,
  input  [2:0] Sel,
  output [3:0] Probe1
);

  wire clk_out, sysclk_out;

  Clock clk (.out(clk_out));
  Universal universal_1 (.clk(clk_out), .Reset(Reset), .Sel(Sel), .out_4(Probe1));
  Hex_Digit_Display hex_digit_display_1 (.value(Probe1));  // open: dp
  Clock #(.highDuration(16), .lowDuration(16)) sysclk (.out(sysclk_out));
  // Digital_Oscilloscope digital_oscilloscope_1: pin names not known; wires that end beside it: sysclk_out, clk_out, Probe1[0], Probe1[1], Probe1[2], Probe1[3]
endmodule

module Universal (
  input  clk,
  input  Reset,
  input  [2:0] Sel,
  output [3:0] out_4
);

  wire [3:0] async_counter_1_up, async_decade_counter_1_decade, async_down_counter_1_down,
       sync_johnson_counter_1_johnson, sync_ring_counter_1_ring;

  async_counter async_counter_1 (.clk(clk), .Reset(Reset), .Up(async_counter_1_up));
  async_down_counter async_down_counter_1 (.clk(clk), .Reset(Reset), .Down(async_down_counter_1_down));
  async_decade_counter async_decade_counter_1 (.clk(clk), .Reset(Reset), .Decade(async_decade_counter_1_decade));
  sync_ring_counter sync_ring_counter_1 (.clk(clk), .Reset(Reset), .Ring(sync_ring_counter_1_ring));
  sync_johnson_counter sync_johnson_counter_1 (.clk(clk), .Reset(Reset), .Johnson(sync_johnson_counter_1_johnson));
  Multiplexer #(.select(3), .width(4)) multiplexer_1 (
    .in0(async_counter_1_up), .in1(async_down_counter_1_down), .in2(async_decade_counter_1_decade),
    .in3(sync_ring_counter_1_ring), .in4(sync_johnson_counter_1_johnson),
    .in5(sync_johnson_counter_1_johnson), .in6(sync_johnson_counter_1_johnson),
    .in7(sync_johnson_counter_1_johnson), .out(out_4), .sel(Sel));
endmodule

module async_counter (
  input  clk,
  input  Reset,
  output [3:0] Up
);

  wire d_ff_1_qn, d_ff_2_qn, d_ff_3_qn, d_ff_4_qn;

  D_Flip_Flop d_ff_1 (.D(d_ff_1_qn), .clk(clk), .Q(Up[0]), .Qn(d_ff_1_qn), .reset(Reset));  // open: preset
  D_Flip_Flop d_ff_2 (.D(d_ff_2_qn), .clk(d_ff_1_qn), .Q(Up[1]), .Qn(d_ff_2_qn), .reset(Reset));  // open: preset
  D_Flip_Flop d_ff_3 (.D(d_ff_3_qn), .clk(d_ff_2_qn), .Q(Up[2]), .Qn(d_ff_3_qn), .reset(Reset));  // open: preset
  D_Flip_Flop d_ff_4 (.D(d_ff_4_qn), .clk(d_ff_3_qn), .Q(Up[3]), .Qn(d_ff_4_qn), .reset(Reset));  // open: preset
endmodule

module async_down_counter (
  input  clk,
  input  Reset,
  output [3:0] Down
);

  wire d_ff_1_qn, d_ff_2_qn, d_ff_3_qn, d_ff_4_qn, undriven;

  D_Flip_Flop d_ff_1 (.D(d_ff_1_qn), .clk(clk), .Q(Down[0]), .Qn(d_ff_1_qn), .preset(Reset));  // open: reset
  D_Flip_Flop d_ff_2 (.D(d_ff_2_qn), .clk(Down[0]), .Q(Down[1]), .Qn(d_ff_2_qn), .preset(Reset), .reset(undriven));
  D_Flip_Flop d_ff_3 (.D(d_ff_3_qn), .clk(Down[1]), .Q(Down[2]), .Qn(d_ff_3_qn), .preset(Reset));  // open: reset
  D_Flip_Flop d_ff_4 (.D(d_ff_4_qn), .clk(Down[2]), .Q(Down[3]), .Qn(d_ff_4_qn), .preset(Reset));  // open: reset
endmodule

module async_decade_counter (
  input  clk,
  input  Reset,
  output [3:0] Decade
);

  wire and_1_out, d_ff_1_qn, d_ff_2_qn, d_ff_3_qn, d_ff_4_qn, or_1_out;

  D_Flip_Flop d_ff_1 (.D(d_ff_1_qn), .clk(clk), .Q(Decade[0]), .Qn(d_ff_1_qn), .reset(or_1_out));  // open: preset
  or or_1 (or_1_out, Reset, and_1_out);
  D_Flip_Flop d_ff_2 (.D(d_ff_2_qn), .clk(d_ff_1_qn), .Q(Decade[1]), .Qn(d_ff_2_qn), .reset(or_1_out));  // open: preset
  D_Flip_Flop d_ff_3 (.D(d_ff_3_qn), .clk(d_ff_2_qn), .Q(Decade[2]), .Qn(d_ff_3_qn), .reset(or_1_out));  // open: preset
  D_Flip_Flop d_ff_4 (.D(d_ff_4_qn), .clk(d_ff_3_qn), .Q(Decade[3]), .Qn(d_ff_4_qn), .reset(or_1_out));  // open: preset
  and and_1 (and_1_out, Decade[3], Decade[1]);
endmodule

module sync_ring_counter (
  input  clk,
  input  Reset,
  output [3:0] Ring
);

  wire d_ff_4_qn;

  D_Flip_Flop d_ff_1 (.D(Ring[3]), .clk(clk), .Q(Ring[0]), .preset(Reset));  // open: Qn, reset
  D_Flip_Flop d_ff_2 (.D(Ring[0]), .clk(clk), .Q(Ring[1]), .reset(Reset));  // open: Qn, preset
  D_Flip_Flop d_ff_3 (.D(Ring[1]), .clk(clk), .Q(Ring[2]), .reset(Reset));  // open: Qn, preset
  D_Flip_Flop d_ff_4 (.D(Ring[2]), .clk(clk), .Q(Ring[3]), .Qn(d_ff_4_qn), .reset(Reset));  // open: preset
endmodule

module sync_johnson_counter (
  input  clk,
  input  Reset,
  output [3:0] Johnson
);

  wire d_ff_4_qn;

  D_Flip_Flop d_ff_1 (.D(d_ff_4_qn), .clk(clk), .Q(Johnson[0]), .preset(Reset));  // open: Qn, reset
  D_Flip_Flop d_ff_2 (.D(Johnson[0]), .clk(clk), .Q(Johnson[1]), .reset(Reset));  // open: Qn, preset
  D_Flip_Flop d_ff_3 (.D(Johnson[1]), .clk(clk), .Q(Johnson[2]), .reset(Reset));  // open: Qn, preset
  D_Flip_Flop d_ff_4 (.D(Johnson[2]), .clk(clk), .Q(Johnson[3]), .Qn(d_ff_4_qn), .reset(Reset));  // open: preset
endmodule
