// Logisim project Bekzat_Kabdrashev_counter.circ as structural Verilog
module One_bit_adder (
  input  A,
  input  B,
  input  C_in,
  output Sum,
  output C_out
);

  wire and_1_out, and_2_out, and_3_out, xor_1_out;

  and and_1 (and_1_out, A, B);
  xor xor_1 (xor_1_out, A, B);
  and and_2 (and_2_out, B, C_in);
  and and_3 (and_3_out, A, C_in);
  xor xor_2 (Sum, xor_1_out, C_in);
  or or_1 (C_out, and_2_out, and_1_out, and_3_out);
endmodule

module Two_bit_adder (
  input  A1,
  input  B1,
  input  A0,
  input  B0,
  input  C_in,
  output Sum1,
  output C_out,
  output Sum0
);

  wire one_bit_adder_1_c_out;

  One_bit_adder one_bit_adder_1 (.A(A0), .B(B0), .C_in(C_in), .Sum(Sum0), .C_out(one_bit_adder_1_c_out));
  One_bit_adder one_bit_adder_2 (.A(A1), .B(B1), .C_in(one_bit_adder_1_c_out), .Sum(Sum1), .C_out(C_out));
endmodule

module Two_bit_counter (
  input  in_1,
  output Out1,
  output Out0
);

  wire clock_1_out, two_bit_adder_1_sum0, two_bit_adder_1_sum1;

  Two_bit_adder two_bit_adder_1 (
    .A1(Out1), .B1(1'b0), .A0(Out0), .B0(1'b1), .C_in(in_1), .Sum1(two_bit_adder_1_sum1),
    .Sum0(two_bit_adder_1_sum0));  // open: C_out
  Clock clock_1 (.out(clock_1_out));
  D_Flip_Flop d_ff_1 (.D(two_bit_adder_1_sum1), .clk(clock_1_out), .Q(Out1));  // open: Qn, preset, reset
  D_Flip_Flop d_ff_2 (.D(two_bit_adder_1_sum0), .clk(clock_1_out), .Q(Out0));  // open: Qn, preset, reset
endmodule
