// Logisim project 8bit_CPU.circ as structural Verilog: 5 circuits, main circuit main
module main (
);

  wire and_1_out, and_2_out, clock_1_out, not_1_out, simple_decoder_1_wen;
  wire [1:0] simple_decoder_1_opcode, simple_decoder_1_rd, simple_decoder_1_rs1, simple_decoder_1_rs2;
  wire [3:0] pc_1_addrout, register_file_1_r0out, register_file_1_r0out_2, register_file_1_r1out,
       register_file_1_r1out_2, register_file_1_r2out, register_file_1_r2out_2, register_file_1_r3out,
       register_file_1_r3out_2, simple_decoder_1_addr, simple_decoder_1_imm, simple_rom_1_out_2,
       simple_rom_1_out_2_2;
  wire [7:0] adder_1_out, multiplexer_1_out, not_2_out, register_file_1_rdata1, register_file_1_rdata2,
       xor_1_out;

  Clock clock_1 (.out(clock_1_out));
  Hex_Digit_Display hex_digit_display_1 (.value(pc_1_addrout));  // open: dp
  PC pc_1 (.Addr(simple_decoder_1_addr), .isAddr(and_1_out), .clk(clock_1_out), .AddrOut(pc_1_addrout));
  Hex_Digit_Display hex_digit_display_2 (.value(simple_rom_1_out_2_2));  // open: dp
  Hex_Digit_Display hex_digit_display_3 (.value(simple_rom_1_out_2));  // open: dp
  // Probe on {simple_rom_1_out_2_2, simple_rom_1_out_2}
  Simple_rom simple_rom_1 (.Addr(pc_1_addrout), .out_2({simple_rom_1_out_2_2, simple_rom_1_out_2}));
  Adder adder_1 (.a(register_file_1_rdata1), .b(register_file_1_rdata2), .out(adder_1_out));  // open: cin, cout
  and and_1 (and_1_out, simple_decoder_1_opcode[0], not_1_out, simple_decoder_1_opcode[1]);
  Simple_decoder simple_decoder_1 (
    .Inst({simple_rom_1_out_2_2, simple_rom_1_out_2}), .rd(simple_decoder_1_rd), .rs1(simple_decoder_1_rs1),
    .rs2(simple_decoder_1_rs2), .imm(simple_decoder_1_imm), .opcode(simple_decoder_1_opcode),
    .wen(simple_decoder_1_wen), .Addr(simple_decoder_1_addr));
  Hex_Digit_Display hex_digit_display_4 (.value(register_file_1_rdata2[7:4]));  // open: dp
  Hex_Digit_Display hex_digit_display_5 (.value(register_file_1_rdata2[3:0]));  // open: dp
  Multiplexer #(.select(2), .width(8)) multiplexer_1 (
    .in0(adder_1_out), .in2({4'b0000, simple_decoder_1_imm}), .out(multiplexer_1_out),
    .sel(simple_decoder_1_opcode));  // open: in1, in3
  Hex_Digit_Display hex_digit_display_6 (.value(register_file_1_rdata1[7:4]));  // open: dp
  Hex_Digit_Display hex_digit_display_7 (.value(register_file_1_rdata1[3:0]));  // open: dp
  // Probe on register_file_1_rdata1
  // Probe on register_file_1_rdata2
  Register_file register_file_1 (
    .wen(simple_decoder_1_wen), .wdata(multiplexer_1_out), .rs1(simple_decoder_1_rs1),
    .rd(simple_decoder_1_rd), .rs2(simple_decoder_1_rs2), .clk(clock_1_out), .rdata1(register_file_1_rdata1),
    .rdata2(register_file_1_rdata2), .R0out({register_file_1_r0out_2, register_file_1_r0out}),
    .R1out({register_file_1_r1out_2, register_file_1_r1out}),
    .R2out({register_file_1_r2out_2, register_file_1_r2out}),
    .R3out({register_file_1_r3out_2, register_file_1_r3out}));
  Hex_Digit_Display hex_digit_display_8 (.value(register_file_1_r0out_2));  // open: dp
  not not_1 (not_1_out, and_2_out);
  Hex_Digit_Display R0 (.value(register_file_1_r0out));  // open: dp
  Hex_Digit_Display hex_digit_display_9 (.value(register_file_1_r1out_2));  // open: dp
  // Probe on {register_file_1_r0out_2, register_file_1_r0out}
  Hex_Digit_Display hex_digit_display_10 (.value(register_file_1_r1out));  // open: dp
  Hex_Digit_Display hex_digit_display_11 (.value(register_file_1_r2out_2));  // open: dp
  // Probe on {register_file_1_r1out_2, register_file_1_r1out}
  assign xor_1_out = register_file_1_rdata2 ^ {register_file_1_r0out_2, register_file_1_r0out};  // XOR_Gate xor_1, 8 bits wide
  assign not_2_out = ~xor_1_out;  // NOT_Gate not_2, 8 bits wide
  Hex_Digit_Display hex_digit_display_12 (.value(register_file_1_r2out));  // open: dp
  Hex_Digit_Display hex_digit_display_13 (.value(register_file_1_r3out_2));  // open: dp
  // Probe on {register_file_1_r2out_2, register_file_1_r2out}
  Hex_Digit_Display hex_digit_display_14 (.value(register_file_1_r3out));  // open: dp
  // Probe on {register_file_1_r3out_2, register_file_1_r3out}
  and and_2 (and_2_out, not_2_out[0], not_2_out[1], not_2_out[2], not_2_out[3], not_2_out[4], not_2_out[5], not_2_out[6], not_2_out[7]);

  // Notes on the sheet:
  //   PC
  //   Instruction
  //   RS1
  //   RS2
  //   R0
  //   R1
  //   R2
  //   R3
endmodule

module PC (
  input  [3:0] Addr,
  input  isAddr,
  input  clk,
  output [3:0] AddrOut
);

  wire [3:0] adder_1_out, multiplexer_1_out;

  Adder #(.width(4)) adder_1 (.a(AddrOut), .b(4'b0001), .out(adder_1_out));  // open: cin, cout
  Multiplexer #(.width(4)) multiplexer_1 (.in0(adder_1_out), .in1(Addr), .out(multiplexer_1_out), .sel(isAddr));
  Register #(.width(4)) register_1 (.D(multiplexer_1_out), .clk(clk), .Q(AddrOut));  // open: en, clr
endmodule

module Simple_decoder (
  input  [7:0] Inst,
  output [1:0] rd,
  output [1:0] rs1,
  output [1:0] rs2,
  output [3:0] imm,
  output [1:0] opcode,
  output wen,
  output [3:0] Addr
);

  Multiplexer #(.select(2)) multiplexer_1 (.in0(1'b1), .in1(1'b1), .in2(1'b1), .in3(1'b0), .out(wen), .sel(Inst[7:6]));

  assign Addr = Inst[5:2];
  assign imm = Inst[3:0];
  assign opcode = Inst[7:6];
  assign rd = Inst[5:4];
  assign rs1 = Inst[3:2];
  assign rs2 = Inst[1:0];
endmodule

module Simple_rom (
  input  [3:0] Addr,
  output [7:0] out_2
);

  Multiplexer #(.select(4), .width(8)) multiplexer_1 (
    .in0(8'h8a), .in1(8'h90), .in2(8'ha0), .in3(8'hb1), .in4(8'h17), .in5(8'h29), .in6(8'hd1), .in7(8'hdf),
    .in8({8{1'b1}}), .in9({8{1'b1}}), .in10({8{1'b1}}), .in11({8{1'b1}}), .in12({8{1'b1}}), .in13({8{1'b1}}),
    .in14({8{1'b1}}), .in15({8{1'b1}}), .out(out_2), .sel(Addr));
endmodule

module Register_file (
  input  wen,
  input  [7:0] wdata,
  input  [1:0] rs1,
  input  [1:0] rd,
  input  [1:0] rs2,
  input  clk,
  output [7:0] rdata1,
  output [7:0] rdata2,
  output [7:0] R0out,
  output [7:0] R1out,
  output [7:0] R2out,
  output [7:0] R3out
);

  wire demultiplexer_1_out0, demultiplexer_1_out1, demultiplexer_1_out2, demultiplexer_1_out3;

  Demultiplexer #(.select(2)) demultiplexer_1 (
    .out0(demultiplexer_1_out0), .out1(demultiplexer_1_out1), .out2(demultiplexer_1_out2),
    .out3(demultiplexer_1_out3), .in(wen), .sel(rd));
  Register R0 (.D(wdata), .en(demultiplexer_1_out0), .clk(clk), .Q(R0out));  // open: clr
  Register R1 (.D(wdata), .en(demultiplexer_1_out1), .clk(clk), .Q(R1out));  // open: clr
  Register R2 (.D(wdata), .en(demultiplexer_1_out2), .clk(clk), .Q(R2out));  // open: clr
  Register R3 (.D(wdata), .en(demultiplexer_1_out3), .clk(clk), .Q(R3out));  // open: clr
  Multiplexer #(.select(2), .width(8)) multiplexer_1 (
    .in0(R0out), .in1(R1out), .in2(R2out), .in3(R3out), .out(rdata1), .sel(rs1));
  Multiplexer #(.select(2), .width(8)) multiplexer_2 (
    .in0(R0out), .in1(R1out), .in2(R2out), .in3(R3out), .out(rdata2), .sel(rs2));
endmodule
